// Logisim project cpu.circ as structural Verilog: 1 circuit, main circuit main
module main (
  input  [7:0] in_1,
  input  [15:0] in_2,
  input  in_3,
  input  in_4,
  input  DATA_TO_IR,
  input  ADDR_TO_IP,
  input  IP_INC,
  input  IP_TO_ADDR,
  input  DATA_TO_A,
  input  A_TO_DATA,
  input  A_TO_X,
  input  ADDR_TO_MAR,
  input  MAR_INC,
  input  SUB,
  input  Z_TO_DATA,
  input  MDR_TO_DATA,
  input  DATA_TO_MDR,
  input  FLAGS,
  input  ADDR_TO_HL,
  input  HL_TO_ADDR,
  input  DATA_TO_Y,
  input  ADDR_TO_HL_2,
  input  DATA_TO_B,
  input  T_TO_ADDR,
  input  B_TO_DATA,
  input  DATA_TO_C,
  input  C_TO_DATA,
  input  ADDR_TO_SP,
  input  SP_DEC,
  input  SP_TO_ADDR,
  input  SP_INC,
  input  DATA_TO_D,
  input  D_TO_DATA,
  input  DATA_TO_ADDR_HI,
  input  ADDR_HI_TO_DATA,
  input  DATA_TO_ADDR_LO,
  input  ADDR_LO_TO_DATA,
  output [7:0] out_38,
  output [15:0] out_39,
  output [15:0] out_40,
  output [7:0] out_41,
  output [7:0] out_42,
  output [15:0] out_43,
  output [7:0] out_44,
  output [7:0] out_45,
  output [7:0] out_46,
  output [7:0] out_47,
  output [7:0] out_48,
  output [15:0] out_49,
  output [7:0] _C_Z,
  output [15:0] out_51,
  output [7:0] out_52,
  output [7:0] out_53,
  output [15:0] out_54,
  output [7:0] out_55,
  output [7:0] out_56
);

  wire adder_1_cout, and_1_out, and_2_out, and_3_out, and_4_out, and_5_out, and_6_out, and_7_out, and_8_out,
       CLK, nor_1_out, not_1_out, or_1_out, or_2_out, or_3_out, or_4_out, or_5_out, or_6_out, or_7_out,
       or_8_out, or_9_out, or_10_out, RST;
  wire [7:0] bit_extender_1_out, xor_1_out;

  Button u_CLK (.out(CLK));
  Button u_RST (.out(RST));
  assign bit_extender_1_out = {{7{SUB}}, SUB};  // Bit_Extender bit_extender_1
  Register register_1 (.D(out_38), .en(DATA_TO_IR), .Q(out_41), .clk(CLK), .clr(RST));
  Register register_2 (.D(out_38), .en(DATA_TO_A), .Q(out_42), .clk(CLK));  // open: clr
  assign out_38 = A_TO_DATA ? out_42 : 8'bz;  // Controlled_Buffer controlled_buffer_1
  Register register_3 (.D(out_42), .en(A_TO_X), .Q(out_44), .clk(CLK));  // open: clr
  Adder adder_1 (.a(out_44), .b(xor_1_out), .out(out_45), .cin(SUB), .cout(adder_1_cout));
  assign xor_1_out = bit_extender_1_out ^ out_52;  // XOR_Gate xor_1, 8 bits wide
  Register register_4 (.D(out_38), .en(DATA_TO_Y), .Q(out_52), .clk(CLK));  // open: clr
  assign out_38 = B_TO_DATA ? out_53 : 8'bz;  // Controlled_Buffer controlled_buffer_2
  Register register_5 (.D(out_38), .en(DATA_TO_B), .Q(out_53), .clk(CLK));  // open: clr
  assign out_38 = C_TO_DATA ? out_55 : 8'bz;  // Controlled_Buffer controlled_buffer_3
  Register register_6 (.D(out_38), .en(DATA_TO_C), .Q(out_55), .clk(CLK));  // open: clr
  Register register_7 (.D(out_38), .en(DATA_TO_D), .Q(out_56), .clk(CLK));  // open: clr
  assign out_38 = D_TO_DATA ? out_56 : 8'bz;  // Controlled_Buffer controlled_buffer_4
  assign out_38 = Z_TO_DATA ? out_45 : 8'bz;  // Controlled_Buffer controlled_buffer_5
  nor nor_1 (nor_1_out, out_45[0], out_45[1], out_45[2], out_45[3], out_45[4], out_45[5], out_45[6], out_45[7]);
  D_Flip_Flop d_ff_1 (.clk(CLK), .D(nor_1_out), .Q(_C_Z[0]), .en(FLAGS), .reset(RST));  // open: Qn, preset
  D_Flip_Flop d_ff_2 (.clk(CLK), .D(adder_1_cout), .Q(_C_Z[1]), .en(FLAGS), .reset(RST));  // open: Qn, preset
  assign out_38 = in_3 ? in_1 : 8'bz;  // Controlled_Buffer controlled_buffer_6
  assign out_46 = DATA_TO_MDR ? out_38 : 8'bz;  // Controlled_Buffer controlled_buffer_7
  assign out_38 = MDR_TO_DATA ? out_46 : 8'bz;  // Controlled_Buffer controlled_buffer_8
  assign out_39[7:0] = DATA_TO_ADDR_LO ? out_38 : 8'bz;  // Controlled_Buffer controlled_buffer_9
  assign out_39[15:8] = DATA_TO_ADDR_HI ? out_38 : 8'bz;  // Controlled_Buffer controlled_buffer_10
  not not_1 (not_1_out, DATA_TO_MDR);
  or or_1 (or_1_out, ADDR_TO_SP, SP_DEC);
  or or_2 (or_2_out, SP_DEC, SP_INC);
  Counter #(.width(16), .max('hffff)) counter_1 (
    .load(ADDR_TO_IP), .D(out_39), .count(IP_INC), .Q(out_40), .clk(CLK), .clr(RST));  // open: carry
  Counter #(.width(16), .max('hffff)) counter_2 (
    .load(ADDR_TO_MAR), .D(out_39), .count(MAR_INC), .Q(out_43), .clk(CLK));  // open: carry, clr
  Register #(.width(16)) register_8 (.D(out_39), .en(ADDR_TO_HL), .Q({out_48, out_47}), .clk(CLK));  // open: clr
  Register #(.width(16)) register_9 (.D(out_39), .en(ADDR_TO_HL_2), .Q(out_51), .clk(CLK));  // open: clr
  Counter #(.width(16), .max('hffff)) counter_3 (
    .load(or_1_out), .D(out_39), .count(or_2_out), .Q(out_54), .clk(CLK), .clr(RST));  // open: carry
  RAM #(.addrWidth(16)) ram_1 (.addr(out_43), .data(out_46), .sel(1'b1), .clk(CLK), .ld(not_1_out));  // open: clr
  assign out_39[7:0] = or_3_out ? out_40[7:0] : 8'bz;  // Controlled_Buffer controlled_buffer_11
  and and_1 (and_1_out, ADDR_TO_IP, DATA_TO_ADDR_HI);
  or or_3 (or_3_out, and_1_out, IP_TO_ADDR);
  and and_2 (and_2_out, ADDR_TO_IP, DATA_TO_ADDR_LO);
  or or_4 (or_4_out, IP_TO_ADDR, and_2_out);
  assign out_39[7:0] = or_5_out ? out_47 : 8'bz;  // Controlled_Buffer controlled_buffer_12
  and and_3 (and_3_out, ADDR_TO_HL, DATA_TO_ADDR_HI);
  or or_5 (or_5_out, and_3_out, HL_TO_ADDR);
  and and_4 (and_4_out, ADDR_TO_HL, DATA_TO_ADDR_LO);
  or or_6 (or_6_out, HL_TO_ADDR, and_4_out);
  assign out_39[7:0] = or_7_out ? out_51[7:0] : 8'bz;  // Controlled_Buffer controlled_buffer_13
  and and_5 (and_5_out, ADDR_TO_HL_2, DATA_TO_ADDR_HI);
  or or_7 (or_7_out, and_5_out, T_TO_ADDR);
  or or_8 (or_8_out, T_TO_ADDR, and_6_out);
  and and_6 (and_6_out, ADDR_TO_HL_2, DATA_TO_ADDR_LO);
  assign out_39[7:0] = or_9_out ? out_54[7:0] : 8'bz;  // Controlled_Buffer controlled_buffer_14
  and and_7 (and_7_out, ADDR_TO_SP, DATA_TO_ADDR_HI);
  or or_9 (or_9_out, and_7_out, SP_TO_ADDR);
  and and_8 (and_8_out, ADDR_TO_SP, DATA_TO_ADDR_LO);
  or or_10 (or_10_out, SP_TO_ADDR, and_8_out);
  assign out_38 = ADDR_HI_TO_DATA ? out_39[15:8] : 8'bz;  // Controlled_Buffer controlled_buffer_15
  assign out_39[15:8] = or_4_out ? out_40[15:8] : 8'bz;  // Controlled_Buffer controlled_buffer_16
  assign out_39[15:8] = or_6_out ? out_48 : 8'bz;  // Controlled_Buffer controlled_buffer_17
  assign out_39[15:8] = or_8_out ? out_51[15:8] : 8'bz;  // Controlled_Buffer controlled_buffer_18
  assign out_39[15:8] = or_10_out ? out_54[15:8] : 8'bz;  // Controlled_Buffer controlled_buffer_19
  assign out_38 = ADDR_LO_TO_DATA ? out_39[7:0] : 8'bz;  // Controlled_Buffer controlled_buffer_20
  assign out_39 = in_4 ? in_2 : 16'bz;  // Controlled_Buffer controlled_buffer_21

  assign _C_Z[7:2] = {6{1'b0}};
  assign out_49 = {out_48, out_47};

  // Other names for the same wires on the sheet: ZF = _C_Z[0]; CF = _C_Z[1]

  // Notes on the sheet:
  //   A Register
  //   X Register
  //   Y Register
  //   B Register
  //   C Register
  //   D Register
  //   Instruction Register
  //   Adder / Subtractor
  //   Flags
  //   8-Bit Data Bus
  //   Z Register
  //   Memory Address Register
  //   L Register
  //   H Register
  //   Instruction Pointer
  //   Memory Data Register
  //   HL Register
  //   T Register
  //   Stack Pointer
  //   16-Bit Address Bus
endmodule
